// Logisim project gorbit-ram.circ as structural Verilog: 3 circuits, main circuit main
module main (
);

  wire addrsel, aluop, branch, charrdy, clk, clock_1_out, incrpc, loadir, loadmem, loadpc, loadptr, loadx,
       nextchar, or_1_out, putchar, waitchar;
  wire [1:0] dsel;
  wire [6:0] keyboard_1_data;
  wire [7:0] addr, aluout, charinput, data, IR_q, memout, PC_q, PTR_q, xreg;

  TTY tty_1 (.data(data[6:0]), .clk(clk), .we(putchar));  // open: clr
  Keyboard keyboard_1 (.clk(clk), .re(nextchar), .avail(charrdy), .data(keyboard_1_data));  // open: clr
  Counter #(.ongoal("stay")) PC (.load(loadpc), .D(memout), .count(incrpc), .Q(PC_q), .clk(clk));  // open: carry, clr
  Register PTR (.D(memout), .en(loadptr), .Q(PTR_q), .clk(clk));  // open: clr
  Multiplexer #(.select(2), .width(8), .enable("false")) multiplexer_1 (
    .in0(memout), .in1(charinput), .in2(aluout), .in3(xreg), .out(data), .sel(dsel));
  Multiplexer #(.width(8), .enable("false")) multiplexer_2 (.in0(PC_q), .in1(PTR_q), .out(addr), .sel(addrsel));
  assign charinput = {{1{1'b0}}, keyboard_1_data};  // Bit_Extender bit_extender_1
  Register IR (.D(memout), .en(loadir), .Q(IR_q), .clk(clk));  // open: clr
  Clock clock_1 (.out(clock_1_out));
  Register X (.D(data), .en(loadx), .Q(xreg), .clk(clk));  // open: clr
  alu ALU (.A(xreg), .B(memout), .op(aluop), .branch(branch), .out(aluout));
  RAM #(.bus("separate")) ram_1 (
    .addr(addr), .din(data), .data(memout), .str(loadmem), .clk(clk), .ld(1'b1));  // open: sel, clr
  con con_1 (
    .branch(branch), .instruction(IR_q[3:0]), .clk(clk), .dsel(dsel), .aluop(aluop), .incrpc(incrpc),
    .loadptr(loadptr), .loadpc(loadpc), .loadx(loadx), .loadmem(loadmem), .loadir(loadir),
    .nextchar(nextchar), .putchar(putchar), .waitchar(waitchar), .addrsel(addrsel));
  and and_1 (clk, clock_1_out, or_1_out);
  or or_1 (or_1_out, ~waitchar, charrdy);  // OR_Gate
endmodule

module alu (
  input  [7:0] A,
  input  [7:0] B,
  input  op,
  output branch,
  output [7:0] out
);

  wire [7:0] adder_1_out, xor_1_out;

  Adder adder_1 (.a(A), .b(B), .out(adder_1_out));  // open: cin, cout
  assign xor_1_out = B ^ A;  // XOR_Gate xor_1, 8 bits wide
  Multiplexer #(.width(8), .enable("false")) multiplexer_1 (.in0(adder_1_out), .in1(xor_1_out), .out(out), .sel(op));
  nor nor_1 (branch, A[0], A[1], A[2], A[3], A[4], A[5], A[6], A[7]);
endmodule

module con (
  input  branch,
  input  [3:0] instruction,
  input  clk,
  output [1:0] dsel,
  output addrsel,
  output aluop,
  output incrpc,
  output loadptr,
  output loadpc,
  output loadx,
  output loadmem,
  output loadir,
  output nextchar,
  output putchar,
  output waitchar
);

  wire and_1_out, d_ff_1_q;
  wire [1:0] T_State_q;
  wire [9:0] rom_1_data;

  Counter #(.width(2), .max('h3)) T_State (.Q(T_State_q), .clk(clk), .clr(d_ff_1_q));  // open: load, D, count, carry
  D_Flip_Flop d_ff_1 (.clk(clk), .D(rom_1_data[0]), .Q(d_ff_1_q), .reset(d_ff_1_q));  // open: Qn, preset, en
  ROM #(.addrWidth(6), .dataWidth(14)) rom_1 (
    .addr({instruction, T_State_q}),
    .data({dsel, addrsel, aluop, rom_1_data[9:8], loadptr, loadx, loadmem, loadir, nextchar, putchar, waitchar, rom_1_data[0]}));  // open: sel
  // Probe on rom_1_data[0]
  and and_1 (and_1_out, ~branch, rom_1_data[8]);  // AND_Gate
  or or_1 (incrpc, and_1_out, rom_1_data[9]);
  and and_2 (loadpc, rom_1_data[8], branch);

  // Notes on the sheet:
  //   Microcode
  //   contents of rom_1 (hex, n*v repeats v):
  //   210 80 a41 0 210 80 3a21 0 210 2 1249 0 210 101 0 0 210 2241 0 0 210 3205 0 0 210 241 0 0 210 80
  //   2a41 0 210 80 880 a41 210 80 880 3a21 210 82 1a29 0 210 80 901 0 210 80 2a21 0 210 80 a05 0 210 80
  //   2e41 0 210 80 880 2a41
  //   Branch logic
endmodule
